# Fritzing sketch tracker (saved by Fritzing 0.9.3b)

parts:
  U2 = Wemos Lolin D32
  SD_card_module1 = SD Card Module
  BATT1 = LiPoly Battery (1300mAh)
  Bauteil1 = u-blox NEO-6M GPS Breakout

nets:
  N1: U2.pin_0, SD_card_module1.+3.3, Bauteil1.VCC
  N2: U2.pin_16, U2.pin_17, BATT1.positive, BATT1.negative
  GND: U2.pin_18, U2.pin_33, SD_card_module1.GND, Bauteil1.GND
  N3: U2.pin_22, SD_card_module1.CS
  N4: U2.pin_23, Bauteil1.RXD
  N5: U2.pin_24, Bauteil1.TXD
  N6: U2.pin_26, SD_card_module1.SCK
  N7: U2.pin_27, SD_card_module1.MISO
  N8: U2.pin_32, SD_card_module1.MOSI

custom parts:
  Wemos Lolin D32: Wemos Lolin D32 wifi and blue tooth board based on the ESP-32 cpu, digital I/Os 22, analog inputs 6, analog outputs 2 clock 240mhz, Flash 4Mbytes, lipo battery charger (500ma connection broken out on breadboard but not pcb), usb. The mounting holes are only set on the silkscreen, if you want actual holes in the pcb copy the hole from the pcb menu in parts over the top of the hole in the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
  SD Card Module: SD Card Module Slot Socket Reader For Arduino ARM MCU
  LiPoly Battery (1300mAh): Lithium Ion Polymer Battery (1300mAh)
